// Logisim project ex2.circ as structural Verilog: 6 circuits, main circuit AND2
module AND2 (
  input  A,
  input  B,
  output RESULT
);

  and and_1 (RESULT, A, B);

  // Notes on the sheet:
  //   Sample Circuit
endmodule

module NAND2 (
  input  A,
  input  B,
  output RESULT
);

  wire and_1_out;

  and and_1 (and_1_out, A, B);
  not not_1 (RESULT, and_1_out);
endmodule

module NOR2 (
  input  A,
  input  B,
  output RESULT
);

  wire or_1_out;

  or or_1 (or_1_out, A, B);
  not not_1 (RESULT, or_1_out);
endmodule

module XOR2 (
  input  A,
  input  B,
  output RESULT
);

  wire and_1_out, not_1_out, or_1_out;

  or or_1 (or_1_out, A, B);
  and and_1 (and_1_out, A, B);
  not not_1 (not_1_out, and_1_out);
  and and_2 (RESULT, or_1_out, not_1_out);
endmodule

module MUX2 (
  input  A,
  input  B,
  input  SEL,
  output RESULT
);

  wire and_1_out, and_2_out, not_1_out;

  not not_1 (not_1_out, SEL);
  and and_1 (and_1_out, B, SEL);
  and and_2 (and_2_out, A, not_1_out);
  or or_1 (RESULT, and_2_out, and_1_out);
endmodule

module MUX4 (
  input  A,
  input  B,
  input  C,
  input  D,
  input  SEL0,
  input  SEL1,
  output RESULT
);

  wire and2_1_result, and2_2_result, and_1_out, and_2_out, and_3_out, and_4_out, and_5_out, and_6_out,
       nand2_1_result, not_1_out, not_2_out, or_1_out, or_2_out, xor2_1_result, xor2_2_result;

  XOR2 xor2_1 (.A(SEL1), .B(SEL0), .RESULT(xor2_1_result));
  NAND2 nand2_1 (.A(SEL0), .B(SEL1), .RESULT(nand2_1_result));
  not not_1 (not_1_out, xor2_2_result);
  XOR2 xor2_2 (.A(SEL0), .B(SEL1), .RESULT(xor2_2_result));
  not not_2 (not_2_out, nand2_1_result);
  and and_1 (and_1_out, B, and_2_out);
  and and_2 (and_2_out, xor2_1_result, SEL0);
  and and_3 (and_3_out, xor2_1_result, SEL1);
  and and_4 (and_4_out, and_3_out, C);
  AND2 and2_1 (.A(nand2_1_result), .B(not_1_out), .RESULT(and2_1_result));
  AND2 and2_2 (.A(not_1_out), .B(not_2_out), .RESULT(and2_2_result));
  or or_1 (or_1_out, and_1_out, and_4_out);
  and and_5 (and_5_out, A, and2_1_result);
  and and_6 (and_6_out, D, and2_2_result);
  or or_2 (or_2_out, and_5_out, and_6_out);
  or or_3 (RESULT, or_2_out, or_1_out);
endmodule
