// Logisim project ex5.circ as structural Verilog: 1 circuit, main circuit num_checker
module num_checker (
  input  [31:0] num,
  input  clk,
  output is_odd,
  output is_even,
  output is_zero,
  output greater_than_fifteen,
  output five_or_ten
);

  wire and_1_out, and_2_out, comparator_5_eq, comparator_6_eq, comparator_7_eq, comparator_8_eq,
       comparator_9_eq, comparator_10_eq;
  wire [7:0] adder_1_out, register_1_q;

  Register register_1 (.D(adder_1_out), .clk(clk), .Q(register_1_q));  // open: en, clr
  Adder adder_1 (.a(register_1_q), .b(8'h1), .out(adder_1_out));  // open: cin, cout
  Comparator #(.mode("unsigned"), .width(1)) comparator_1 (.a(num[0]), .b(1'b1), .eq(is_odd));  // open: gt, lt
  Comparator #(.mode("unsigned"), .width(1)) comparator_2 (.a(num[0]), .b(1'b0), .eq(is_even));  // open: gt, lt
  Comparator #(.mode("unsigned"), .width(32)) comparator_3 (.a(num), .b({32{1'b0}}), .eq(is_zero));  // open: gt, lt
  Comparator #(.mode("unsigned"), .width(32)) comparator_4 (
    .a(num), .b(32'hf), .gt(greater_than_fifteen));  // open: eq, lt
  Comparator #(.width(3)) comparator_5 (.a(num[2:0]), .b(3'b111), .eq(comparator_5_eq));  // open: gt, lt
  Comparator #(.width(29)) comparator_6 (.a(num[31:3]), .b({29{1'b0}}), .eq(comparator_6_eq));  // open: gt, lt
  Comparator #(.width(2)) comparator_7 (.b(2'b11), .eq(comparator_7_eq));  // open: a, gt, lt
  Comparator #(.width(30)) comparator_8 (.b({30{1'b0}}), .eq(comparator_8_eq));  // open: a, gt, lt
  and and_1 (and_1_out, comparator_5_eq, comparator_6_eq);
  and and_2 (and_2_out, comparator_7_eq, comparator_8_eq);
  Comparator #(.mode("unsigned"), .width(3)) comparator_9 (
    .a(num[2:0]), .b(3'b101), .eq(comparator_9_eq));  // open: gt, lt
  Comparator #(.mode("unsigned"), .width(5)) comparator_10 (
    .a(num[4:0]), .b(5'b01010), .eq(comparator_10_eq));  // open: gt, lt
  // OR_Gate or_1 has open pins: in0=and_1_out, in1=and_2_out, out=open
  or or_2 (five_or_ten, comparator_9_eq, comparator_10_eq);

  // Other names for the same wires on the sheet: bit_zero = num[0]; bits_five[2:0] = num[2:0];
  //   bits_ten[4:0] = num[4:0]; five_rest_zero[28:0] = num[31:3]; bits_15[27:0] = num[31:4]
endmodule
